// Logisim project ControlUnit.circ as structural Verilog: 1 circuit, main circuit main
module main (
  input  [3:0] Opcode,
  output [2:0] ALUctr,
  output ALUsrc,
  output RegWrite,
  output MemWrite,
  output ExtOp,
  output MemtoReg,
  output Branch,
  output RegDst
);

  wire and_1_out, and_2_out, and_3_out, and_4_out, and_5_out, and_6_out, and_7_out, not_1_out, not_2_out,
       not_3_out, not_4_out;
  wire [2:2] not_5_out;

  not not_1 (not_1_out, Opcode[0]);
  not not_2 (not_2_out, Opcode[1]);
  not not_3 (not_3_out, Opcode[2]);
  not not_4 (not_4_out, Opcode[3]);
  and and_1 (and_1_out, not_1_out, not_2_out, not_3_out, not_4_out);
  and and_2 (and_2_out, Opcode[0], not_2_out, not_3_out, not_4_out);
  and and_3 (and_3_out, not_1_out, Opcode[1], not_3_out, not_4_out);
  and and_4 (and_4_out, Opcode[0], Opcode[1], not_3_out, not_4_out);
  and and_5 (and_5_out, not_1_out, not_2_out, Opcode[2], not_4_out);
  and and_6 (and_6_out, Opcode[0], not_2_out, Opcode[2], not_4_out);
  and and_7 (and_7_out, not_1_out, Opcode[1], Opcode[2], not_4_out);
  and and_8 (MemWrite, Opcode[0], Opcode[1], Opcode[2], not_4_out);
  and and_9 (MemtoReg, not_1_out, not_2_out, not_4_out, Opcode[3]);
  and and_10 (Branch, Opcode[0], not_2_out, not_4_out, Opcode[3]);
  or or_1 (RegDst, and_1_out, and_2_out, and_3_out, and_4_out, and_6_out, and_7_out);
  // OR_Gate or_2 has open pins: in0=MemtoReg, in1=MemWrite, in2=and_5_out, out=open
  or or_3 (ALUsrc, and_5_out, MemWrite, MemtoReg);
  or or_4 (RegWrite, and_6_out, and_2_out, and_3_out, and_4_out, and_5_out, and_1_out, MemtoReg, and_7_out);
  or or_5 (ExtOp, MemWrite, MemtoReg);
  not not_5 (not_5_out[2], MemWrite);
  Multiplexer #(.width(3)) multiplexer_1 (
    .in0(Opcode[2:0]), .in1({3{not_5_out[2]}}), .out(ALUctr), .sel(MemWrite));  // open: en

  // Notes on the sheet:
  //   Add
  //   Sub
  //   mul
  //   Div
  //   ori
  //   nor
  //   nand
  //   sw
  //   lw
  //   blt
endmodule
