// Logisim project ALU.circ as structural Verilog: 1 circuit, main circuit main
module main (
  input  [15:0] A,
  input  [15:0] B,
  input  [2:0] ALUselect,
  output ZERO,
  output [15:0] result
);

  wire [15:0] adder_1_out, divider_1_out, multiplier_1_out, nand_1_out, nor_1_out, or_1_out, subtractor_1_out;

  Adder #(.width(16)) adder_1 (.a(A), .b(B), .out(adder_1_out));  // open: cin, cout
  Subtractor #(.width(16)) subtractor_1 (.a(A), .b(B), .out(subtractor_1_out));  // open: bin, bout
  Multiplier #(.width(16)) multiplier_1 (.a(A), .b(B), .out(multiplier_1_out));  // open: cin, cout
  Divider #(.width(16)) divider_1 (.a(A), .b(B), .out(divider_1_out));  // open: upper, rem
  assign or_1_out = A | B;  // OR_Gate or_1, 16 bits wide
  assign nor_1_out = ~(A | B);  // NOR_Gate nor_1, 16 bits wide
  assign nand_1_out = ~(A & B);  // NAND_Gate nand_1, 16 bits wide
  Multiplexer #(.select(3), .width(16), .enable("false")) multiplexer_1 (
    .in0(adder_1_out), .in1(subtractor_1_out), .in2(multiplier_1_out), .in3(divider_1_out), .in4(or_1_out),
    .in5(nor_1_out), .in6(nand_1_out), .out(result), .sel(ALUselect));  // open: in7
  nor nor_2 (ZERO, result[0], result[1], result[2], result[3], result[4], result[5], result[6], result[7], result[8], result[9], result[10], result[11], result[12], result[13], result[14], result[15]);
endmodule
