// Logisim project CPU.circ as structural Verilog: 1 circuit, main circuit main
module main (
  input  in_1
);

  wire ALUsrc, and_1_out, Branch, CLK, comparator_1_gt, ExtOp, MemRead, MemToReg, MemWrite, RegDst, RegWrite;
  wire [2:0] AluCtr;
  wire [3:0] multiplexer_1_out;
  wire [15:0] adder_1_out, adder_2_out, bit_extender_1_out, bit_extender_2_out, main_2_read_data_1,
       main_2_read_data_2, main_3_result, multiplexer_2_out, multiplexer_3_out, multiplexer_4_out,
       multiplexer_5_out, PC_q, ram_1_data, rom_1_data, shifter_1_out;

  Register #(.width(16)) PC (.D(multiplexer_5_out), .Q(PC_q), .clk(CLK), .clr(in_1));  // open: en
  Clock clock_1 (.out(CLK));
  ControlUnit_main main_1 (
    .Opcode(rom_1_data[15:12]), .ALUctr(AluCtr), .MemWrite(MemWrite), .ExtOp(ExtOp), .MemtoReg(MemToReg),
    .Branch(Branch), .RegDst(RegDst), .ALUsrc(ALUsrc), .RegWrite(RegWrite), .MemRead(MemRead));
  ROM #(.addrWidth(16), .dataWidth(16)) rom_1 (.addr(PC_q), .data(rom_1_data));  // open: sel
  Multiplexer #(.width(4), .enable("false")) multiplexer_1 (
    .in0(rom_1_data[7:4]), .in1(rom_1_data[3:0]), .out(multiplexer_1_out), .sel(RegDst));
  Adder #(.width(16)) adder_1 (.a(16'h1), .b(PC_q), .out(adder_1_out));  // open: cin, cout
  assign bit_extender_1_out = {{12{1'b0}}, rom_1_data[3:0]};  // Bit_Extender bit_extender_1
  assign bit_extender_2_out = {{12{rom_1_data[3]}}, rom_1_data[3:0]};  // Bit_Extender bit_extender_2
  Multiplexer #(.width(16), .enable("false")) multiplexer_2 (
    .in0(bit_extender_1_out), .in1(bit_extender_2_out), .out(multiplexer_2_out), .sel(ExtOp));
  RegisterFile_main main_2 (
    .Write_data(multiplexer_4_out), .Read_data_1(main_2_read_data_1), .Read_data_2(main_2_read_data_2),
    .Write_register(multiplexer_1_out), .RegWrite(RegWrite), .Read_register_1(rom_1_data[11:8]),
    .Read_register_2(rom_1_data[7:4]), .CLK(CLK), .Clear(in_1));
  Shifter #(.width(16)) shifter_1 (.in(multiplexer_2_out), .\dist (4'b0001), .out(shifter_1_out));
  Multiplexer #(.width(16), .enable("false")) multiplexer_3 (
    .in0(main_2_read_data_2), .in1(multiplexer_2_out), .out(multiplexer_3_out), .sel(ALUsrc));
  ALU_main main_3 (
    .A(main_2_read_data_1), .B(multiplexer_3_out), .result(main_3_result), .Opcode(AluCtr));  // open: ZERO
  Adder #(.width(16)) adder_2 (.a(adder_1_out), .b(shifter_1_out), .out(adder_2_out));  // open: cin, cout
  Comparator #(.width(16)) comparator_1 (.a({16{1'b0}}), .b(main_3_result), .gt(comparator_1_gt));  // open: eq, lt
  and and_1 (and_1_out, Branch, comparator_1_gt);
  Multiplexer #(.width(16), .enable("false")) multiplexer_4 (
    .in0(main_3_result), .in1(ram_1_data), .out(multiplexer_4_out), .sel(MemToReg));
  RAM #(.addrWidth(16), .dataWidth(16), .bus("separate")) ram_1 (
    .addr(main_3_result), .din(main_2_read_data_2), .data(ram_1_data), .str(MemWrite), .clk(CLK),
    .ld(MemRead), .clr(in_1));  // open: sel
  Multiplexer #(.width(16), .enable("false")) multiplexer_5 (
    .in0(adder_1_out), .in1(adder_2_out), .out(multiplexer_5_out), .sel(and_1_out));

  // Other names for the same wires on the sheet: Clr = in_1

  // Notes on the sheet:
  //   contents of rom_1 (hex, n*v repeats v):
  //   402a 403f 327 1328 7230 7271 7282 8290 82a1 82b2 9238
endmodule
